# Fritzing sketch newtypecircuit (saved by Fritzing 0.9.3b)
circuit board: 8.46667cm x 5.64444cm
breadboards: 1

parts:
  INPUT = BNC [package=bnc]
  U2 = OP37 - Low Noise, Precision, High Speed Op Amp [part_number=OP37]
  U3 = OP37 - Low Noise, Precision, High Speed Op Amp [part_number=OP37]
  U4 = OP37 - Low Noise, Precision, High Speed Op Amp [part_number=OP37]
  R1 = Resistor [tolerance=±5% resistance=220 package=THT]
  R2 = Resistor [tolerance=±5% resistance=220 package=THT]
  R3 = Resistor [tolerance=±5% resistance=220 package=THT]
  R4 = Resistor [tolerance=±5% resistance=220 package=THT]
  R5 = Resistor [tolerance=±5% resistance=220 package=THT]
  R6 = Resistor [tolerance=±5% resistance=220 package=THT]
  OUTPUT = BNC [package=bnc]
  R7 = Resistor [tolerance=±5% resistance=220 package=THT]
  4 = female pin header, 1 pin [form="♀ (female)"]
  7 = female pin header, 1 pin [form="♀ (female)"]
  Ground = female pin header, 1 pin [form="♀ (female)"]
  C1 = Tantalum Capacitor [capacitance=10µF package="100 mil [THT, tantalum]"]
  100_nF = Tantalum Capacitor [capacitance=1μF package="100 mil [THT, tantalum]"]
  C3 = Tantalum Capacitor [capacitance=100nF package="100 mil [THT, tantalum]"]
  C4 = Tantalum Capacitor [capacitance=10µF package="100 mil [THT, tantalum]"]
  J1 = female pin header, 1 pin [form="♀ (female)"]

nets:
  N1: INPUT.GND, U3.+IN
  N2: INPUT.OUT, U2.+IN
  N3: U2.-IN, R1.Pin_0, R3.Pin_0
  N4: U2.-V, U3.-V, U4.-V, 4.pin1, C1.+, 100_nF.+
  N5: U2.OUT, R3.Pin_1, R4.Pin_0
  N6: U2.V+, U3.V+, U4.V+, 7.pin1, C3.+, C4.+
  N7: U3.-IN, R1.Pin_1, R2.Pin_0
  N8: U3.OUT, R2.Pin_1, R5.Pin_0
  N9: U4.-IN, R4.Pin_1, R7.Pin_0
  N10: U4.+IN, R5.Pin_1, R6.Pin_0
  N11: U4.OUT, OUTPUT.OUT, R7.Pin_1
  N12: R6.Pin_1, OUTPUT.GND, Ground.pin1, C1.-, 100_nF.-, C3.-, C4.-, J1.pin1
