# Fritzing sketch remakechargeampTwinTCR (saved by Fritzing 0.9.3b)
circuit board: 8.47cm x 5.64444cm
breadboards: 1

parts:
  U1 = OP27 - Low Noise, Precision Op Amp [part_number=OP27]
  C1 = Tantalum Capacitor [capacitance=1nF package="100 mil [THT, tantalum]"]
  R1 = Resistor [tolerance=±5% resistance=1G package=THT]
  4 = female pin header, 1 pin [form="♀ (female)"]
  7 = female pin header, 1 pin [form="♀ (female)"]
  J5 = female pin header, 2 pins [form="♀ (female)"]
  J6 = female pin header, 1 pin [form="♀ (female)"]
  J7 = female pin header, 1 pin [form="♀ (female)"]
  GND = female pin header, 2 pins [form="♀ (female)"]
  R2 = Resistor [tolerance=±5% resistance=100M package=THT]
  R3 = Resistor [tolerance=±5% resistance=10M package=THT]
  R4 = Resistor [tolerance=±5% resistance=1M package=THT]
  C2 = Tantalum Capacitor [capacitance=10nF package="100 mil [THT, tantalum]"]
  C3 = Tantalum Capacitor [capacitance=100nF package="100 mil [THT, tantalum]"]
  C4 = Tantalum Capacitor [capacitance=1μF package="100 mil [THT, tantalum]"]
  R5 = Resistor [tolerance=±5% resistance=30k package=THT]
  R6 = Resistor [tolerance=±5% resistance=1k package=THT]
  R7 = Resistor [tolerance=±5% resistance=300 package=THT]
  R8 = Resistor [tolerance=±5% resistance=300 package=THT]
  C5 = Tantalum Capacitor [capacitance=220nF package="100 mil [THT, tantalum]"]
  C6 = Tantalum Capacitor [capacitance=100nF package="100 mil [THT, tantalum]"]
  R9 = Resistor [tolerance=±5% resistance=30k package=THT]
  R10 = Resistor [tolerance=±5% resistance=1k package=THT]
  R11 = Resistor [tolerance=±5% resistance=300 package=THT]
  R12 = Resistor [tolerance=±5% resistance=300 package=THT]
  C7 = Tantalum Capacitor [capacitance=100nF package="100 mil [THT, tantalum]"]
  R13 = Resistor [tolerance=±5% resistance=15k package=THT]
  R14 = Resistor [tolerance=±5% resistance=820 package=THT]
  J15 = female pin header, 1 pin [form="♀ (female)"]
  C8 = Tantalum Capacitor [capacitance=100nF package="100 mil [THT, tantalum]"]
  C9 = Tantalum Capacitor [capacitance=10µF package="100 mil [THT, tantalum]"]
  C10 = Tantalum Capacitor [capacitance=100nF package="100 mil [THT, tantalum]"]
  C11 = Tantalum Capacitor [capacitance=10µF package="100 mil [THT, tantalum]"]
  1 = female pin header, 1 pin [form="♀ (female)"]
  2 = female pin header, 1 pin [form="♀ (female)"]
  3 = female pin header, 1 pin [form="♀ (female)"]
  1_2 = female pin header, 1 pin [form="♀ (female)"]  # not connected
  2_2 = female pin header, 1 pin [form="♀ (female)"]  # not connected
  3_2 = female pin header, 1 pin [form="♀ (female)"]  # not connected
  INPUT = BNC [package=bnc]
  OUTPUT = BNC [package=bnc]
  1_3 = female pin header, 1 pin [form="♀ (female)"]
  2_3 = female pin header, 1 pin [form="♀ (female)"]
  3_3 = female pin header, 1 pin [form="♀ (female)"]
  1_4 = female pin header, 1 pin [form="♀ (female)"]  # not connected
  2_4 = female pin header, 1 pin [form="♀ (female)"]  # not connected
  3_4 = female pin header, 1 pin [form="♀ (female)"]  # not connected

nets:
  N1: U1.-IN, C1.+, R1.Pin_0, INPUT.OUT
  GND: U1.+IN, J5.pin1, J5.pin2, J6.pin1, J7.pin1, GND.pin1, GND.pin2, C5.+, R14.Pin_1, J15.pin1, C8.-, C9.-, C10.-, C11.-, 1.pin1, 2.pin1, 3.pin1, INPUT.GND, OUTPUT.GND, 1_3.pin1, 2_3.pin1, 3_3.pin1
  N2: U1.-V, 4.pin1, C8.+, C9.+
  N3: U1.OUT, C1.-, R1.Pin_1, R2.Pin_1, R3.Pin_1, R4.Pin_1, C2.+, C3.+, C4.+, R5.Pin_0, C6.-
  N4: U1.V+, 7.pin1, C10.+, C11.+
  N5: R5.Pin_1, R6.Pin_0
  N6: R6.Pin_1, R7.Pin_0
  N7: R7.Pin_1, R8.Pin_0
  N8: R8.Pin_1, C5.-, R9.Pin_0
  N9: C6.+, C7.-, R13.Pin_0
  N10: R9.Pin_1, R10.Pin_0
  N11: R10.Pin_1, R11.Pin_0
  N12: R11.Pin_1, R12.Pin_0
  N13: R12.Pin_1, C7.+, OUTPUT.OUT
  N14: R13.Pin_1, R14.Pin_0
